# Fritzing sketch alexaLights (saved by Fritzing 0.9.3b)
breadboards: 1

parts:
  Q1 = npn-Powertransistor [part_number=TIP120 package="TO220 [THT]"]
  J1 = Screw terminal - 2 pins [package=THT]
  J2 = Screw terminal - 2 pins [package=THT]
  Part1 = Photon
  R1 = Resistor [tolerance=±10% resistance=1k package=THT]
  D2 = Rectifier Diode [part_number=1N4001 package="Melf DO-213 AB [SMD]"]
  PIR1 = PIR sensor

nets:
  N1: Q1.base, R1.Pin_1
  N2: Q1.collector, J1.pin1, D2.cathode
  GND: Q1.emitter, J2.pin2, Part1.GND, D2.anode, PIR1.GND
  N3: J1.pin2, J2.pin1
  VIN: Part1.VIN, PIR1.VDD
  N4: Part1.D1, R1.Pin_0
  N5: Part1.D3, PIR1.SIG

notes:
  INPUT POWER
